// Logisim project projet_etu.circ as structural Verilog: 10 circuits, main circuit main
module main (
  input  Reset,
  input  ResetRAM
);

  wire ALUEnable, and_1_out, and_2_out, Clock, Clock_out, Cond, CTRL, Exec, Fetch, IMM, Load, MEM, not_1_out,
       ramctrl_1_memload, ramctrl_1_memstore, Store, WriteReg;
  wire [2:0] GetOp;
  wire [15:0] Addr, alu_1_output, Arg1, Arg2, bit_extender_2_out, condchecker_1_jmpaddress, CSTE, IR, MemIN,
       PC, R0, R1, R2, R3, R4, R5, R6, R7;
  wire [31:0] bit_extender_1_out, MemOUT;

  and and_1 (and_1_out, Exec, Clock);
  Clock u_Clock (.out(Clock_out));
  RegPC regpc_1 (
    .JMP_Address(condchecker_1_jmpaddress), .Cond(Cond), .CTRL(CTRL), .Clock(and_1_out), .Reset(Reset),
    .PC(PC));
  // Probe on PC
  Seq seq_1 (.ClockOrig(Clock_out), .reset(Reset), .Fetch(Fetch), .Exec(Exec), .Clock(Clock));
  LED led_1 (.in(Clock_out));
  GetAddr getaddr_1 (
    .PC(PC), .Addr(Addr), .Fetch(Fetch), .RAMAddr(CSTE), .Arg1(Arg1), .OP(GetOp), .Load(Load), .Store(Store));
  // Probe on Addr
  // Probe on MemIN
  LED led_2 (.in(Fetch));
  LED led_3 (.in(Exec));
  // Probe on GetOp
  assign bit_extender_1_out = {{16{MemIN[15]}}, MemIN};  // Bit_Extender bit_extender_1
  CondChecker condchecker_1 (
    .COND(Cond), .CTRL(CTRL), .OpCode(GetOp), .PC(PC), .CLOCK(Clock), .RESET(Reset),
    .JMPADDRESS(condchecker_1_jmpaddress), .EXEC(Exec), .CSTE(CSTE), .Arg1(Arg1), .Arg2(Arg2));
  RamCtrl ramctrl_1 (
    .Store(Store), .Fetch(Fetch), .Exec(Exec), .Load(Load), .MemStore(ramctrl_1_memstore),
    .MemLoad(ramctrl_1_memload), .Clock(Clock));
  // Probe on PC
  // Probe on {CSTE, IR}
  DecodeIR decodeir_1 (
    .CTRL(CTRL), .WriteReg(WriteReg), .IR({CSTE, IR}), .Load(Load), .GetOp(GetOp), .Store(Store), .MEM(MEM),
    .ALU(ALUEnable), .Immediat(IMM));
  // Probe on CSTE
  // Probe on R0
  // Probe on R3
  // Probe on R6
  // Probe on MemOUT
  RAM #(.addrWidth(16), .dataWidth(32), .bus("separate")) ram_1 (
    .addr(Addr), .din(bit_extender_1_out), .data(MemOUT), .str(ramctrl_1_memstore), .clk(ramctrl_1_memstore),
    .ld(ramctrl_1_memload), .clr(ResetRAM));  // open: sel
  and and_2 (and_2_out, Fetch, Clock);
  // Probe on {CSTE, IR}
  Register #(.width(32), .trigger("high")) RegIR (
    .D(MemOUT), .Q({CSTE, IR}), .clk(and_2_out), .clr(Reset));  // open: en
  // Probe on R1
  // Probe on R4
  // Probe on R7
  // Probe on R2
  // Probe on R5
  Registres registres_1 (
    .SR1(IR[11:9]), .IN(alu_1_output), .SR2(IR[14:12]), .WriteReg(WriteReg), .DR(IR[8:6]), .OUT_SR1(Arg1),
    .OUT_SR2(Arg2), .OUT_DR(MemIN), .R0(R0), .R1(R1), .R2(R2), .R3(R3), .R4(R4), .R5(R5), .R6(R6), .R7(R7),
    .Reset(Reset), .Clock(Exec));
  // Probe on IR[8:6]
  // Probe on IR[11:9]
  // Probe on IR[14:12]
  // Probe on Arg1
  ALU alu_1 (
    .Imm(IMM), .e2(GetOp), .Input1(Arg1), .Input2(Arg2), .Cst(CSTE), .Output(alu_1_output),
    .ALUEnable(ALUEnable));
  // Probe on alu_1_output
  // Probe on Arg2
  Multiplexer #(.width(16)) multiplexer_1 (
    .in0(bit_extender_2_out), .in1(CSTE), .out(alu_1_output), .sel(IMM), .en(not_1_out));
  not not_1 (not_1_out, ALUEnable);
  Bit_Extender #(.in_width(32), .\type ("sign")) bit_extender_2 (.in(MemOUT), .out(bit_extender_2_out));
  // Probe on R0
  // Probe on R1
  // Probe on R2
  // Probe on R3
  // Probe on R4
  // Probe on R5
  // Probe on R6
  // Probe on R7
  // Probe on alu_1_output

  // Other names for the same wires on the sheet: IR[31:16] = CSTE

  // Notes on the sheet:
  //   RAM
endmodule

module ALU (
  input  [15:0] Input1,
  input  [15:0] Input2,
  input  [15:0] Cst,
  input  Imm,
  input  [2:0] e2,
  input  ALUEnable,
  output [15:0] Output
);

  wire [3:0] bit_extender_1_out, bit_extender_2_out;
  wire [15:0] adder_1_out, and_1_out, demultiplexer_1_out0, demultiplexer_1_out1, demultiplexer_1_out2,
       demultiplexer_1_out3, demultiplexer_1_out4, demultiplexer_1_out5, demultiplexer_1_out6,
       demultiplexer_1_out7, demultiplexer_2_out0, demultiplexer_2_out1, demultiplexer_2_out2,
       demultiplexer_2_out3, demultiplexer_2_out4, demultiplexer_2_out5, demultiplexer_2_out6,
       demultiplexer_2_out7, multiplexer_1_out, multiplier_1_out, or_1_out, shifter_1_out, shifter_2_out,
       subtractor_1_out, xor_1_out;

  Demultiplexer #(.select(3), .width(16), .enable("false")) demultiplexer_1 (
    .out0(demultiplexer_1_out0), .out1(demultiplexer_1_out1), .out2(demultiplexer_1_out2),
    .out3(demultiplexer_1_out3), .out4(demultiplexer_1_out4), .out5(demultiplexer_1_out5),
    .out6(demultiplexer_1_out6), .out7(demultiplexer_1_out7), .in(Input1), .sel(e2));
  Multiplexer #(.width(16), .enable("false")) multiplexer_1 (
    .in0(Input2), .in1(Cst), .out(multiplexer_1_out), .sel(Imm));
  Demultiplexer #(.select(3), .width(16), .enable("false")) demultiplexer_2 (
    .out0(demultiplexer_2_out0), .out1(demultiplexer_2_out1), .out2(demultiplexer_2_out2),
    .out3(demultiplexer_2_out3), .out4(demultiplexer_2_out4), .out5(demultiplexer_2_out5),
    .out6(demultiplexer_2_out6), .out7(demultiplexer_2_out7), .in(multiplexer_1_out), .sel(e2));
  Adder #(.width(16)) adder_1 (
    .a(demultiplexer_1_out0), .b(demultiplexer_2_out0), .out(adder_1_out));  // open: cin, cout
  Subtractor #(.width(16)) subtractor_1 (
    .a(demultiplexer_1_out1), .b(demultiplexer_2_out1), .out(subtractor_1_out));  // open: bin, bout
  assign and_1_out = demultiplexer_1_out2 & demultiplexer_2_out2;  // AND_Gate and_1, 16 bits wide
  assign or_1_out = demultiplexer_1_out3 | demultiplexer_2_out3;  // OR_Gate or_1, 16 bits wide
  assign xor_1_out = demultiplexer_1_out4 ^ demultiplexer_2_out4;  // XOR_Gate xor_1, 16 bits wide
  Shifter #(.width(16)) shifter_1 (.in(demultiplexer_1_out5), .\dist (bit_extender_1_out), .out(shifter_1_out));
  Bit_Extender #(.in_width(16), .out_width(4), .\type ("sign")) bit_extender_1 (
    .in(demultiplexer_2_out5), .out(bit_extender_1_out));
  Shifter #(.width(16), .shift("lr")) shifter_2 (
    .in(demultiplexer_1_out6), .\dist (bit_extender_2_out), .out(shifter_2_out));
  Bit_Extender #(.in_width(16), .out_width(4), .\type ("sign")) bit_extender_2 (
    .in(demultiplexer_2_out6), .out(bit_extender_2_out));
  Multiplier #(.width(16)) multiplier_1 (
    .a(demultiplexer_1_out7), .b(demultiplexer_2_out7), .out(multiplier_1_out));  // open: cin, cout
  Multiplexer #(.select(3), .width(16)) multiplexer_2 (
    .in0(adder_1_out), .in1(subtractor_1_out), .in2(and_1_out), .in3(or_1_out), .in4(xor_1_out),
    .in5(shifter_1_out), .in6(shifter_2_out), .in7(multiplier_1_out), .out(Output), .sel(e2), .en(ALUEnable));
endmodule

module DecodeIR (
  input  [31:0] IR,
  output CTRL,
  output ALU,
  output WriteReg,
  output Store,
  output MEM,
  output Load,
  output Immediat,
  output [2:0] GetOp
);

  and and_1 (CTRL, IR[0], IR[1]);
  and and_2 (ALU, ~IR[0], ~IR[1]);  // AND_Gate
  and and_3 (MEM, ~IR[0], IR[1]);  // AND_Gate
  and and_4 (Store, MEM, IR[4]);
  and and_5 (Load, MEM, ~IR[4]);  // AND_Gate
  or or_1 (WriteReg, ALU, Load);

  assign GetOp = IR[4:2];
  assign Immediat = IR[5];
endmodule

module GetAddr (
  input  [15:0] PC,
  input  Fetch,
  input  [15:0] Arg1,
  input  [15:0] RAMAddr,
  input  [2:0] OP,
  input  Store,
  input  Load,
  output [15:0] Addr
);

  wire [15:0] multiplexer_1_out;

  Multiplexer #(.width(16), .enable("false")) multiplexer_1 (
    .in0(Arg1), .in1(RAMAddr), .out(multiplexer_1_out), .sel(OP[0]));
  Multiplexer #(.width(16), .enable("false")) multiplexer_2 (
    .in0(multiplexer_1_out), .in1(PC), .out(Addr), .sel(Fetch));
endmodule

module GetCst (
  input  [31:0] IR,
  output [15:0] Cst,
  output Imm
);


  assign Cst = IR[31:16];
  assign Imm = IR[5];
endmodule

module RamCtrl (
  input  Clock,
  input  Exec,
  input  Fetch,
  input  Load,
  input  Store,
  output MemLoad,
  output MemStore
);

  wire and_1_out;

  and and_1 (and_1_out, Exec, Load);
  and and_2 (MemStore, Exec, Clock, Store);
  or or_1 (MemLoad, Fetch, and_1_out);
endmodule

module Registres (
  input  [15:0] IN,
  input  [2:0] SR1,
  input  WriteReg,
  input  [2:0] SR2,
  input  [2:0] DR,
  input  Clock,
  input  Reset,
  output [15:0] R0,
  output [15:0] OUT_SR1,
  output [15:0] R1,
  output [15:0] R2,
  output [15:0] R3,
  output [15:0] OUT_SR2,
  output [15:0] R4,
  output [15:0] R5,
  output [15:0] R6,
  output [15:0] OUT_DR,
  output [15:0] R7
);

  wire decoder_1_out0, decoder_1_out1, decoder_1_out2, decoder_1_out3, decoder_1_out4, decoder_1_out5,
       decoder_1_out6, decoder_1_out7;

  Decoder #(.select(3), .disabled(0)) decoder_1 (
    .out0(decoder_1_out0), .out1(decoder_1_out1), .out2(decoder_1_out2), .out3(decoder_1_out3),
    .out4(decoder_1_out4), .out5(decoder_1_out5), .out6(decoder_1_out6), .out7(decoder_1_out7), .sel(DR),
    .en(WriteReg));
  Register #(.width(16), .trigger("falling")) u_R0 (.D(IN), .en(decoder_1_out0), .Q(R0), .clk(Clock), .clr(Reset));
  Register #(.width(16), .trigger("falling")) u_R1 (.D(IN), .en(decoder_1_out1), .Q(R1), .clk(Clock), .clr(Reset));
  Register #(.width(16), .trigger("falling")) u_R2 (.D(IN), .en(decoder_1_out2), .Q(R2), .clk(Clock), .clr(Reset));
  Register #(.width(16), .trigger("falling")) u_R3 (.D(IN), .en(decoder_1_out3), .Q(R3), .clk(Clock), .clr(Reset));
  Register #(.width(16), .trigger("falling")) u_R4 (.D(IN), .en(decoder_1_out4), .Q(R4), .clk(Clock), .clr(Reset));
  Register #(.width(16), .trigger("falling")) u_R5 (.D(IN), .en(decoder_1_out5), .Q(R5), .clk(Clock), .clr(Reset));
  Register #(.width(16), .trigger("falling")) u_R6 (.D(IN), .en(decoder_1_out6), .Q(R6), .clk(Clock), .clr(Reset));
  Register #(.width(16), .trigger("falling")) u_R7 (.D(IN), .en(decoder_1_out7), .Q(R7), .clk(Clock), .clr(Reset));
  Multiplexer #(.select(3), .width(16)) multiplexer_1 (
    .in0(R0), .in1(R1), .in2(R2), .in3(R3), .in4(R4), .in5(R5), .in6(R6), .in7(R7), .out(OUT_SR1), .sel(SR1));  // open: en
  Multiplexer #(.select(3), .width(16)) multiplexer_2 (
    .in0(R0), .in1(R1), .in2(R2), .in3(R3), .in4(R4), .in5(R5), .in6(R6), .in7(R7), .out(OUT_SR2), .sel(SR2));  // open: en
  Multiplexer #(.select(3), .width(16)) multiplexer_3 (
    .in0(R0), .in1(R1), .in2(R2), .in3(R3), .in4(R4), .in5(R5), .in6(R6), .in7(R7), .out(OUT_DR), .sel(DR));  // open: en
endmodule

module RegPC (
  input  [15:0] JMP_Address,
  input  Cond,
  input  CTRL,
  input  Clock,
  input  Reset,
  output [15:0] PC
);

  wire and_1_out;
  wire [15:0] adder_1_out, multiplexer_1_out;

  Multiplexer #(.width(16), .enable("false")) multiplexer_1 (
    .in0(adder_1_out), .in1(JMP_Address), .out(multiplexer_1_out), .sel(and_1_out));
  and and_1 (and_1_out, Cond, CTRL);
  Adder #(.width(16)) adder_1 (.a(16'h1), .b(PC), .out(adder_1_out));  // open: cin, cout
  Register #(.width(16)) register_1 (.D(multiplexer_1_out), .Q(PC), .clk(Clock), .clr(Reset));  // open: en
endmodule

module Seq (
  input  ClockOrig,
  input  reset,
  output Fetch,
  output Exec,
  output Clock
);

  Register #(.width(1), .trigger("falling")) register_1 (
    .D(Fetch), .Q(Exec), .clk(ClockOrig), .clr(reset));  // open: en
  not not_1 (Fetch, Exec);
  buf buffer_1 (Clock, ClockOrig);
endmodule

module CondChecker (
  input  [15:0] Arg1,
  input  [15:0] Arg2,
  input  [2:0] OpCode,
  input  RESET,
  input  [15:0] CSTE,
  input  [15:0] PC,
  input  EXEC,
  input  CTRL,
  input  CLOCK,
  output COND,
  output [15:0] JMPADDRESS
);

  wire and_1_out, and_2_out, and_3_out, and_4_out, and_5_out, CLOCK_t, comparator_1_eq, comparator_1_gt,
       comparator_1_lt, or_1_out;
  wire [15:0] adder_1_out, counter_1_q, ram_1_data;

  and and_1 (and_1_out, OpCode[1], OpCode[2]);
  // Probe on and_1_out
  Comparator #(.width(16)) comparator_1 (
    .a(Arg1), .b(Arg2), .gt(comparator_1_gt), .eq(comparator_1_eq), .lt(comparator_1_lt));
  and and_2 (and_2_out, OpCode[0], and_1_out);
  and and_3 (and_3_out, ~OpCode[0], and_1_out);  // AND_Gate
  Adder #(.width(16)) adder_1 (.a(PC), .b(16'h1), .out(adder_1_out));  // open: cin, cout
  or or_1 (or_1_out, comparator_1_gt, comparator_1_lt);
  // Probe on and_2_out
  // Probe on and_3_out
  and and_4 (and_4_out, and_3_out, and_5_out);
  and and_5 (and_5_out, EXEC, CTRL);
  Counter #(.width(16), .max('hffff)) counter_1 (
    .load(and_2_out), .count(1'b1), .Q(counter_1_q), .clk(and_5_out), .clr(RESET));  // open: D, carry
  buf and_6 (CLOCK_t, CLOCK);  // AND_Gate
  RAM #(.addrWidth(16), .dataWidth(16), .bus("separate")) ram_1 (
    .addr(counter_1_q), .din(adder_1_out), .data(ram_1_data), .str(and_3_out), .clk(and_4_out),
    .ld(and_2_out), .clr(RESET));  // open: sel
  Multiplexer #(.width(16), .enable("false")) multiplexer_1 (
    .in0(CSTE), .in1(ram_1_data), .out(JMPADDRESS), .sel(and_2_out));
  Multiplexer #(.select(3), .enable("false")) multiplexer_2 (
    .in0(comparator_1_eq), .in1(or_1_out), .in2(comparator_1_lt), .in3(comparator_1_gt), .in4(1'b1),
    .in6(and_1_out), .in7(and_1_out), .out(COND), .sel(OpCode));  // open: in5
endmodule
